// Logisim project Add_8_bits.circ as structural Verilog: 8 circuits, main circuit main
module main (
  input  [7:0] A,
  input  [7:0] B,
  input  Cin,
  output Cout,
  output Overflow,
  output [7:0] S
);

  Add_8_bits add_8_bits_1 (.A(A), .B(B), .Cin(Cin), .Cout(Cout), .Overflow(Overflow), .S(S));
endmodule

module Add_1_bit (
  input  A,
  input  B,
  input  Cin,
  output S,
  output Cout
);

  wire and_1_out, and_2_out, xor_1_out;

  xor xor_1 (xor_1_out, A, B);
  xor xor_2 (S, xor_1_out, Cin);
  and and_1 (and_1_out, xor_1_out, Cin);
  and and_2 (and_2_out, A, B);
  or or_1 (Cout, and_1_out, and_2_out);
endmodule

module Add_1_bit_OF (
  input  A,
  input  B,
  input  Cin,
  output S,
  output Cout,
  output Overflow
);

  wire and_1_out, and_2_out, xor_1_out;

  xor xor_1 (xor_1_out, A, B);
  xor xor_2 (S, xor_1_out, Cin);
  and and_1 (and_1_out, xor_1_out, Cin);
  and and_2 (and_2_out, A, B);
  or or_1 (Cout, and_1_out, and_2_out);
  xor xor_3 (Overflow, Cout, Cin);
endmodule

module Add_2_bits (
  input  [1:0] A,
  input  [1:0] B,
  input  Cin,
  output Cout,
  output [1:0] S
);

  wire add_1_bit_1_cout;

  Add_1_bit add_1_bit_1 (.S(S[0]), .A(A[0]), .Cout(add_1_bit_1_cout), .Cin(Cin), .B(B[0]));
  Add_1_bit add_1_bit_2 (.S(S[1]), .A(A[1]), .Cout(Cout), .Cin(add_1_bit_1_cout), .B(B[1]));
endmodule

module Add_2_bits_OF (
  input  [1:0] A,
  input  [1:0] B,
  input  Cin,
  output Cout,
  output Overflow,
  output [1:0] S
);

  wire add_1_bit_1_cout;

  Add_1_bit add_1_bit_1 (.S(S[0]), .A(A[0]), .Cout(add_1_bit_1_cout), .Cin(Cin), .B(B[0]));
  Add_1_bit_OF add_1_bit_of_1 (.Cout(Cout), .S(S[1]), .Cin(add_1_bit_1_cout), .B(B[1]), .A(A[1]), .Overflow(Overflow));
endmodule

module Add_4_bits (
  input  [3:0] A,
  input  [3:0] B,
  input  Cin,
  output Cout,
  output [3:0] S
);

  wire add_2_bits_1_cout;

  Add_2_bits add_2_bits_1 (.S(S[1:0]), .Cout(add_2_bits_1_cout), .Cin(Cin), .B(B[1:0]), .A(A[1:0]));
  Add_2_bits add_2_bits_2 (.S(S[3:2]), .Cout(Cout), .Cin(add_2_bits_1_cout), .B(B[3:2]), .A(A[3:2]));
endmodule

module Add_4_bits_OF (
  input  [3:0] A,
  input  [3:0] B,
  input  Cin,
  output Cout,
  output Overflow,
  output [3:0] S
);

  wire add_2_bits_1_cout;

  Add_2_bits add_2_bits_1 (.S(S[1:0]), .Cout(add_2_bits_1_cout), .Cin(Cin), .B(B[1:0]), .A(A[1:0]));
  Add_2_bits_OF add_2_bits_of_1 (
    .Overflow(Overflow), .Cout(Cout), .Cin(add_2_bits_1_cout), .B(B[3:2]), .A(A[3:2]), .S(S[3:2]));
endmodule

module Add_8_bits (
  input  [7:0] A,
  input  [7:0] B,
  input  Cin,
  output Cout,
  output Overflow,
  output [7:0] S
);

  wire add_4_bits_1_cout;

  Add_4_bits add_4_bits_1 (.S(S[3:0]), .A(B[3:0]), .Cout(add_4_bits_1_cout), .B(A[3:0]), .Cin(Cin));
  Add_4_bits_OF add_4_bits_of_1 (
    .Cin(add_4_bits_1_cout), .S(S[7:4]), .Cout(Cout), .B(B[7:4]), .A(A[7:4]), .Overflow(Overflow));
endmodule
