// Logisim project cpu.circ as structural Verilog: 6 circuits, main circuit main
module main (
  input  [15:0] INSTRUCTION,
  input  CLOCK,
  output [15:0] FETCH_ADDRESS,
  output [15:0] L_s0_Value_555821f6,
  output [15:0] L_s1_Value_bb868b5b,
  output [15:0] L_s2_Value_1029e135,
  output [15:0] L_ra_Value_3ae5280b,
  output [15:0] L_sp_Value_256d6ed0,
  output [15:0] L_HI_Value_4d3aacc1,
  output [15:0] L_LO_Value_6d74149f,
  output [3:0] out_11
);

  wire controller_1_clk_out1, controller_1_clk_out2, controller_1_s_m1_alu, controller_1_s_m2_alu,
       controller_1_s_m_reg, controller_1_we_hi, controller_1_we_lo, controller_1_we_reg;
  wire [2:0] controller_1_s_alu, controller_1_s_pc, instruction_decoder_1_funct, instruction_decoder_1_rd,
       instruction_decoder_1_rs, instruction_decoder_1_rt, multiplexer_1_out;
  wire [3:0] instruction_decoder_1_opcode;
  wire [9:0] instruction_decoder_1_immediate;
  wire [15:0] bit_extender_1_out, HO, M, main_1_read_data_1_d638ea5b, main_1_read_data_2_45f3f23e,
       multiplexer_2_out, multiplexer_3_out, multiplexer_4_out, PC2, pc_value_1_pc_out, R, R2,
       wa_value_1_wa_reg;

  Register #(.width(16)) L_PC_1fb09d07 (.D(pc_value_1_pc_out), .en(1'b1), .clk(CLOCK), .Q(FETCH_ADDRESS));  // open: clr
  PC_Value pc_value_1 (
    .PC_out(pc_value_1_pc_out), .PC2_in(PC2), .S_PC(controller_1_s_pc), .PC_in(FETCH_ADDRESS), .JUMP_REG(R),
    .IMM(instruction_decoder_1_immediate));
  PC_Adder pc_adder_1 (.PC_out(PC2), .PC_in(FETCH_ADDRESS));
  Controller controller_1 (
    .S_ALU(controller_1_s_alu), .opcode(instruction_decoder_1_opcode), .funct(instruction_decoder_1_funct),
    .WE_REG(controller_1_we_reg), .clk_in(CLOCK), .clk_out1(controller_1_clk_out1),
    .clk_out2(controller_1_clk_out2), .WE_HI(controller_1_we_hi), .WE_LO(controller_1_we_lo),
    .S_PC(controller_1_s_pc), .S_M1_ALU(controller_1_s_m1_alu), .S_M2_ALU(controller_1_s_m2_alu),
    .S_M_REG(controller_1_s_m_reg), .S_WA_REG(out_11));
  Instruction_decoder instruction_decoder_1 (
    .rd(instruction_decoder_1_rd), .rs(instruction_decoder_1_rs), .funct(instruction_decoder_1_funct),
    .rt(instruction_decoder_1_rt), .immediate(instruction_decoder_1_immediate), .Instruction(INSTRUCTION),
    .opcode(instruction_decoder_1_opcode));
  Multiplexer #(.width(3), .enable("false")) multiplexer_1 (
    .in0(instruction_decoder_1_rt), .in1(instruction_decoder_1_rd), .out(multiplexer_1_out),
    .sel(controller_1_s_m_reg));
  assign bit_extender_1_out = {{6{instruction_decoder_1_immediate[9]}}, instruction_decoder_1_immediate};  // Bit_Extender bit_extender_1
  WA_Value wa_value_1 (
    .S_WA_REG(out_11), .HO(HO), .HI(L_LO_Value_6d74149f), .M(M), .PC2(PC2), .R(R), .WA_REG(wa_value_1_wa_reg));
  regfile_main main_1 (
    .Read_Register_1_a0c8cd62(instruction_decoder_1_rs), .Read_Register_2_6a35ea3b(multiplexer_1_out),
    .Write_Register_a5712683(instruction_decoder_1_rd), .Write_Data_73679b02(wa_value_1_wa_reg),
    .Write_Enable_cb4a62c6(controller_1_we_reg), .Clock(controller_1_clk_out1),
    .Read_Data_1_d638ea5b(main_1_read_data_1_d638ea5b), .Read_Data_2_45f3f23e(main_1_read_data_2_45f3f23e),
    .L_s0_Value_319056dc(L_s0_Value_555821f6), .L_s1_Value_178742e2(L_s1_Value_bb868b5b),
    .L_s2_Value_c4d9ac04(L_s2_Value_1029e135), .L_ra_Value_229931e7(L_ra_Value_3ae5280b),
    .L_sp_Value_102b2bfe(L_sp_Value_256d6ed0));
  Multiplexer #(.width(16), .enable("false")) multiplexer_2 (
    .in0(main_1_read_data_1_d638ea5b), .in1(bit_extender_1_out), .out(multiplexer_2_out),
    .sel(controller_1_s_m1_alu));
  Multiplexer #(.width(16), .enable("false")) multiplexer_3 (
    .in0(16'h6), .in1(bit_extender_1_out), .out(multiplexer_3_out));  // open: sel
  alu_main main_2 (
    .Switch(controller_1_s_alu), .X(multiplexer_2_out), .Result(R), .Y(multiplexer_4_out),
    .Result_2_c6eb2740(R2));  // open: Equal
  Multiplexer #(.width(16), .enable("false")) multiplexer_4 (
    .in0(main_1_read_data_2_45f3f23e), .in1(multiplexer_3_out), .out(multiplexer_4_out),
    .sel(controller_1_s_m2_alu));
  mem_main MEM (.Clock(controller_1_clk_out2), .Read_Data(M));  // open: Address, Write_Data, Write_En
  Register #(.width(16)) L_HI_108849eb (
    .D(R2), .en(controller_1_we_hi), .clk(controller_1_clk_out2), .Q(L_LO_Value_6d74149f));  // open: clr
  Register #(.width(16)) L_LO_6db75bec (
    .D(R), .en(controller_1_we_lo), .clk(controller_1_clk_out2), .Q(L_HI_Value_4d3aacc1));  // open: clr

  // Other names for the same wires on the sheet: clk = CLOCK; fetch_addr[15:0] = FETCH_ADDRESS;
  //   HI[15:0] = L_LO_Value_6d74149f; LO[15:0] = L_HI_Value_4d3aacc1; ra[15:0] = L_ra_Value_3ae5280b;
  //   s0[15:0] = L_s0_Value_555821f6; s1[15:0] = L_s1_Value_bb868b5b; s2[15:0] = L_s2_Value_1029e135;
  //   sp[15:0] = L_sp_Value_256d6ed0

  // Notes on the sheet:
  //   Output
  //   These are outputs/inputs from run.circ
  //   Inputs
  //   These are DEBUG/TEST outputs from your circuit.
endmodule

module Instruction_decoder (
  input  [15:0] Instruction,
  output [2:0] funct,
  output [2:0] rt,
  output [2:0] rs,
  output [9:0] immediate,
  output [2:0] rd,
  output [3:0] opcode
);


  assign funct = Instruction[2:0];
  assign immediate = Instruction[9:0];
  assign opcode = Instruction[15:12];
  assign rd = Instruction[11:9];
  assign rs = Instruction[8:6];
  assign rt = Instruction[5:3];
endmodule

module Controller (
  input  [2:0] funct,
  input  [3:0] opcode,
  input  clk_in,
  output [2:0] S_ALU,
  output clk_out1,
  output [2:0] S_PC,
  output clk_out2,
  output S_M_REG,
  output WE_REG,
  output [3:0] S_WA_REG,
  output WE_HI,
  output WE_LO,
  output S_M1_ALU,
  output S_M2_ALU
);

  wire and_1_out, and_2_out, and_3_out, and_4_out, and_5_out, and_8_out, and_9_out, and_10_out, and_11_out,
       nor_1_out, or_1_out, or_2_out, or_3_out, xnor_1_out;

  or or_1 (or_1_out, ~opcode[0], ~opcode[1]);  // OR_Gate
  Multiplexer #(.select(4), .width(3), .enable("false")) multiplexer_1 (
    .in0(funct), .out(S_ALU), .sel(opcode));  // open: in1, in2, in3, in4, in5, in6, in7, in8, in9, in10, in11, in12, in13, in14, in15
  and and_1 (and_1_out, or_1_out, ~opcode[2]);  // AND_Gate
  or or_2 (or_2_out, and_1_out, opcode[2]);
  and and_2 (and_2_out, funct[0], funct[1], funct[2]);
  nor nor_1 (nor_1_out, opcode[0], opcode[1], opcode[2], opcode[3]);
  and and_3 (and_3_out, or_2_out, opcode[3]);
  or or_3 (or_3_out, and_3_out, and_4_out);
  and and_4 (and_4_out, ~opcode[3], opcode[1]);  // AND_Gate
  and and_5 (and_5_out, nor_1_out, ~and_2_out);  // AND_Gate
  and and_6 (WE_HI, and_2_out, nor_1_out);
  and and_7 (S_M1_ALU, opcode[0], ~opcode[1], ~opcode[2], ~opcode[3]);  // AND_Gate
  or or_4 (WE_REG, or_3_out, and_5_out);
  or or_5 (WE_LO, WE_HI, S_M1_ALU);
  nor nor_2 (S_PC[0], opcode[3], xnor_1_out);
  xnor xnor_1 (xnor_1_out, opcode[1], opcode[2]);
  not not_1 (S_PC[1], opcode[2]);
  and and_8 (and_8_out, ~opcode[3], opcode[2]);  // AND_Gate
  and and_9 (and_9_out, ~opcode[2], ~opcode[1]);  // AND_Gate
  and and_10 (and_10_out, opcode[0], opcode[1], ~opcode[2], opcode[3]);  // AND_Gate
  or or_6 (S_M_REG, and_10_out, and_11_out);
  and and_11 (and_11_out, ~opcode[1], opcode[2], ~opcode[3]);  // AND_Gate
  nor nor_3 (S_WA_REG[0], and_8_out, and_9_out);

  assign clk_out1 = clk_in;
  assign clk_out2 = clk_in;
  assign S_M2_ALU = S_M1_ALU;
  assign S_PC[2] = opcode[0];
  assign S_WA_REG[3:1] = {opcode[0], opcode[2], opcode[3]};
endmodule

module PC_Value (
  input  [15:0] PC2_in,
  input  [15:0] PC_in,
  input  [9:0] IMM,
  input  [2:0] S_PC,
  input  [15:0] JUMP_REG,
  output [15:0] PC_out
);

  wire [15:0] bit_extender_1_out, BRANCH, multiplexer_1_out, multiplexer_3_out;

  assign bit_extender_1_out = {{6{IMM[9]}}, IMM};  // Bit_Extender bit_extender_1
  Adder #(.width(16)) adder_1 (.a(PC_in), .b(bit_extender_1_out), .out(BRANCH));  // open: cin, cout
  Multiplexer #(.width(16), .enable("false")) multiplexer_1 (
    .in0({PC_in[15:10], IMM}), .in1(JUMP_REG), .out(multiplexer_1_out), .sel(S_PC[2]));
  Multiplexer #(.width(16), .enable("false")) multiplexer_2 (
    .in0(PC2_in), .in1(multiplexer_3_out), .out(PC_out), .sel(S_PC[0]));
  Multiplexer #(.width(16), .enable("false")) multiplexer_3 (
    .in0(BRANCH), .in1(multiplexer_1_out), .out(multiplexer_3_out), .sel(S_PC[1]));

  // Other names for the same wires on the sheet: PC[15:0] = PC_in; JUMP[15:0] = JUMP_REG; PC2[15:0] = PC2_in
endmodule

module PC_Adder (
  input  [15:0] PC_in,
  output [15:0] PC_out
);

  Adder #(.width(16)) adder_1 (.a(PC_in), .b(16'h2), .out(PC_out));  // open: cin, cout
endmodule

module WA_Value (
  input  [15:0] R,
  input  [15:0] PC2,
  input  [15:0] M,
  input  [15:0] HI,
  input  [15:0] HO,
  input  [3:0] S_WA_REG,
  output [15:0] WA_REG
);

  wire [15:0] multiplexer_1_out, multiplexer_2_out, multiplexer_3_out;

  Multiplexer #(.width(16), .enable("false")) multiplexer_1 (
    .in0(HI), .in1(HO), .out(multiplexer_1_out), .sel(S_WA_REG[3]));
  Multiplexer #(.width(16), .enable("false")) multiplexer_2 (
    .in0(PC2), .in1(multiplexer_3_out), .out(multiplexer_2_out), .sel(S_WA_REG[1]));
  Multiplexer #(.width(16), .enable("false")) multiplexer_3 (
    .in0(M), .in1(multiplexer_1_out), .out(multiplexer_3_out), .sel(S_WA_REG[2]));
  Multiplexer #(.width(16), .enable("false")) multiplexer_4 (
    .in0(R), .in1(multiplexer_2_out), .out(WA_REG), .sel(S_WA_REG[0]));
endmodule
