// Logisim project mem.circ as structural Verilog: 1 circuit, main circuit main
module main (
  input  [15:0] Address,
  input  Write_En,
  input  Clock,
  input  [15:0] Write_Data,
  output [15:0] Read_Data
);

  RAM #(.addrWidth(14), .dataWidth(16), .databus("bibus")) ram_1 (
    .addr(Address[14:1]), .we(Write_En), .oe(1'b1), .clk(Clock), .din(Write_Data), .dout(Read_Data));
endmodule
