// Logisim project regfile.circ as structural Verilog: 1 circuit, main circuit main
module main (
  input  [2:0] Read_Register_1_a0c8cd62,
  input  [2:0] Read_Register_2_6a35ea3b,
  input  [2:0] Write_Register_a5712683,
  input  [15:0] Write_Data_73679b02,
  input  Write_Enable_cb4a62c6,
  input  Clock,
  output [15:0] L_s0_Value_319056dc,
  output [15:0] L_s1_Value_178742e2,
  output [15:0] L_s2_Value_c4d9ac04,
  output [15:0] L_ra_Value_229931e7,
  output [15:0] L_sp_Value_102b2bfe,
  output [15:0] Read_Data_1_d638ea5b,
  output [15:0] Read_Data_2_45f3f23e
);

  wire demultiplexer_1_out1, demultiplexer_1_out2, demultiplexer_1_out3, demultiplexer_1_out4,
       demultiplexer_1_out5, demultiplexer_1_out6, demultiplexer_1_out7;
  wire [15:0] a0, v0;

  Demultiplexer #(.select(3), .enable("false")) demultiplexer_1 (
    .out1(demultiplexer_1_out1), .out2(demultiplexer_1_out2), .out3(demultiplexer_1_out3),
    .out4(demultiplexer_1_out4), .out5(demultiplexer_1_out5), .out6(demultiplexer_1_out6),
    .out7(demultiplexer_1_out7), .in(Write_Enable_cb4a62c6), .sel(Write_Register_a5712683));  // open: out0
  Register #(.width(16)) ra (
    .D(Write_Data_73679b02), .en(demultiplexer_1_out1), .clk(Clock), .Q(L_ra_Value_229931e7));  // open: clr
  Register #(.width(16)) s0 (
    .D(Write_Data_73679b02), .en(demultiplexer_1_out2), .clk(Clock), .Q(L_s0_Value_319056dc));  // open: clr
  Register #(.width(16)) s1 (
    .D(Write_Data_73679b02), .en(demultiplexer_1_out3), .clk(Clock), .Q(L_s1_Value_178742e2));  // open: clr
  Register #(.width(16)) s2 (
    .D(Write_Data_73679b02), .en(demultiplexer_1_out4), .clk(Clock), .Q(L_s2_Value_c4d9ac04));  // open: clr
  Register #(.width(16)) u_a0 (.D(Write_Data_73679b02), .en(demultiplexer_1_out5), .clk(Clock), .Q(a0));  // open: clr
  Register #(.width(16)) u_v0 (.D(Write_Data_73679b02), .en(demultiplexer_1_out6), .clk(Clock), .Q(v0));  // open: clr
  Register #(.width(16)) sp (
    .D(Write_Data_73679b02), .en(demultiplexer_1_out7), .clk(Clock), .Q(L_sp_Value_102b2bfe));  // open: clr
  Multiplexer #(.select(3), .width(16), .enable("false")) multiplexer_1 (
    .in0({16{1'b0}}), .in1(L_ra_Value_229931e7), .in2(L_s0_Value_319056dc), .in3(L_s1_Value_178742e2),
    .in4(L_s2_Value_c4d9ac04), .in5(a0), .in6(v0), .in7(L_sp_Value_102b2bfe), .out(Read_Data_1_d638ea5b),
    .sel(Read_Register_1_a0c8cd62));
  Multiplexer #(.select(3), .width(16), .enable("false")) multiplexer_2 (
    .in0({16{1'b0}}), .in1(L_ra_Value_229931e7), .in2(L_s0_Value_319056dc), .in3(L_s1_Value_178742e2),
    .in4(L_s2_Value_c4d9ac04), .in5(a0), .in6(v0), .in7(L_sp_Value_102b2bfe), .out(Read_Data_2_45f3f23e),
    .sel(Read_Register_2_6a35ea3b));

  // Other names for the same wires on the sheet: clk = Clock; ra[15:0] = L_ra_Value_229931e7;
  //   read_data1[15:0] = Read_Data_1_d638ea5b; read_data2[15:0] = Read_Data_2_45f3f23e;
  //   read_reg1[2:0] = Read_Register_1_a0c8cd62; read_reg2[2:0] = Read_Register_2_6a35ea3b;
  //   s0[15:0] = L_s0_Value_319056dc; s1[15:0] = L_s1_Value_178742e2; s2[15:0] = L_s2_Value_c4d9ac04;
  //   sp[15:0] = L_sp_Value_102b2bfe; write_data[15:0] = Write_Data_73679b02; write_en = Write_Enable_cb4a62c6;
  //   write_reg[2:0] = Write_Register_a5712683

  // Notes on the sheet:
  //   INPUTS to your circuit
  //   DON'T CHANGE THE LOCATIONS OF THE INPUTS AND OUTPUTS!
  //   These are DEBUG/TEST outputs from your circuit.
  //   OUTPUTS from your circuit
endmodule
