// Logisim project run.circ as structural Verilog: 1 circuit, main circuit main
module main (
  output [15:0] L_s0_Value_f1a4bd28,
  output [15:0] L_s1_Value_91923d1b,
  output [15:0] L_s2_Value_88eac443,
  output [15:0] L_ra_Value_48cc4cd4,
  output [15:0] L_sp_Value_8af3f763,
  output [15:0] L_hi_Value_b95b9feb,
  output [15:0] L_lo_Value_0f321401,
  output [15:0] Time_Step_7eaf1479,
  output [15:0] Requested_Address_d4172265,
  output [15:0] Requested_Instruction_cf0e4866
);

  wire clock_1_out;

  Counter #(.width(16), .max('hffff)) counter_1 (
    .clk(clock_1_out), .Q(Time_Step_7eaf1479));  // open: clr, load, up, count, D, carry
  Clock clock_1 (.out(clock_1_out));
  cpu_main main_1 (
    .INSTRUCTION(Requested_Instruction_cf0e4866), .CLOCK(clock_1_out),
    .FETCH_ADDRESS(Requested_Address_d4172265), .L_s0_Value_555821f6(L_s0_Value_f1a4bd28),
    .L_s1_Value_bb868b5b(L_s1_Value_91923d1b), .L_s2_Value_1029e135(L_s2_Value_88eac443),
    .L_ra_Value_3ae5280b(L_ra_Value_48cc4cd4), .L_LO_Value_6d74149f(L_lo_Value_0f321401),
    .L_HI_Value_4d3aacc1(L_hi_Value_b95b9feb), .L_sp_Value_256d6ed0(L_sp_Value_8af3f763));
  // Probe on Requested_Address_d4172265
  ROM #(.addrWidth(14), .dataWidth(16)) rom_1 (
    .addr(Requested_Address_d4172265[14:1]), .data(Requested_Instruction_cf0e4866));
  // Probe on Requested_Instruction_cf0e4866

  // Other names for the same wires on the sheet: fetch_addr[15:0] = Requested_Address_d4172265;
  //   Instruction[15:0] = Requested_Instruction_cf0e4866

  // Notes on the sheet:
  //   YOUR CPU SHOULD FIT IN HERE!
  //   Instruction Memory
endmodule
