// Logisim project cpu.circ as structural Verilog: 5 circuits, main circuit main
module main (
  input  [15:0] INSTRUCTION,
  input  CLOCK,
  output [15:0] FETCH_ADDRESS,
  output [15:0] L_s0_Value_555821f6,
  output [15:0] L_s1_Value_bb868b5b,
  output [15:0] L_s2_Value_1029e135,
  output [15:0] L_ra_Value_3ae5280b,
  output [15:0] L_sp_Value_256d6ed0,
  output [15:0] L_HI_Value_4d3aacc1,
  output [15:0] L_LO_Value_6d74149f
);

  wire and_1_out, and_2_out, and_3_out, controller_1_s_lo, controller_1_s_pc_bc, controller_1_s_rd,
       controller_1_s_rt, controller_1_s_y, controller_1_we_hi, controller_1_we_lo, controller_1_we_mem,
       controller_1_we_reg, EQUAL, or_1_out;
  wire [2:0] controller_1_s_alu, controller_1_s_imm, controller_1_s_pc, instruction_decoder_1_funct,
       instruction_decoder_1_rd, instruction_decoder_1_rs, instruction_decoder_1_rt;
  wire [3:0] controller_1_s_wa_reg, instruction_decoder_1_opcode;
  wire [15:0] EX_IN_q, IMM, M, main_1_read_data_1_d638ea5b, multiplexer_1_out, multiplexer_2_out,
       multiplexer_3_out, PC2, PC_IN, pc_value_1_pc_out, R, R2, rd, wa_value_1_wa_reg;

  Register #(.width(16)) L_PC_1fb09d07 (.D(pc_value_1_pc_out), .en(1'b1), .clk(CLOCK), .Q(FETCH_ADDRESS));  // open: clr
  Register #(.width(16)) PC_OLD (.D(FETCH_ADDRESS), .en(1'b1), .clk(CLOCK), .Q(PC_IN));  // open: clr
  Adder #(.width(16)) adder_1 (.a(FETCH_ADDRESS), .b(16'h2), .out(PC2));  // open: cin, cout
  PC_Value pc_value_1 (
    .PC_out(pc_value_1_pc_out), .PC2_in(PC2), .S_PC(controller_1_s_pc), .PC_in(PC_IN), .JUMP_REG(R),
    .IMM(IMM), .S_PC_BC(controller_1_s_pc_bc));
  or or_1 (or_1_out, and_1_out, and_2_out);
  and and_1 (and_1_out, ~controller_1_s_pc[1], controller_1_s_pc[0]);  // AND_Gate
  Register #(.width(16)) EX_IN (.D(multiplexer_1_out), .en(1'b1), .clk(CLOCK), .Q(EX_IN_q));  // open: clr
  Multiplexer #(.width(16), .enable("false")) multiplexer_1 (
    .in0(INSTRUCTION), .in1({16{1'b0}}), .out(multiplexer_1_out), .sel(or_1_out));
  and and_2 (and_2_out, and_3_out, controller_1_s_pc_bc);
  and and_3 (and_3_out, controller_1_s_pc[1], controller_1_s_pc[0]);
  Controller controller_1 (
    .S_PC_BC(controller_1_s_pc_bc), .S_RD(controller_1_s_rd), .S_PC(controller_1_s_pc),
    .S_LO(controller_1_s_lo), .S_WA_REG(controller_1_s_wa_reg), .S_RT(controller_1_s_rt),
    .WE_REG(controller_1_we_reg), .S_Y(controller_1_s_y), .S_IMM(controller_1_s_imm), .equal(EQUAL),
    .funct(instruction_decoder_1_funct), .opcode(instruction_decoder_1_opcode), .WE_HI(controller_1_we_hi),
    .WE_MEM(controller_1_we_mem), .WE_LO(controller_1_we_lo), .S_ALU(controller_1_s_alu));
  Instruction_decoder instruction_decoder_1 (
    .rd(instruction_decoder_1_rd), .Instruction(EX_IN_q), .rt(instruction_decoder_1_rt), .immediate(IMM),
    .opcode(instruction_decoder_1_opcode), .funct(instruction_decoder_1_funct),
    .rs(instruction_decoder_1_rs), .S_IMM(controller_1_s_imm), .S_RD(controller_1_s_rd),
    .S_RT(controller_1_s_rt));
  WA_Value wa_value_1 (
    .M(M), .PC2(FETCH_ADDRESS), .S_WA_REG(controller_1_s_wa_reg), .HI(L_HI_Value_4d3aacc1), .R(R),
    .LO(L_LO_Value_6d74149f), .WA_REG(wa_value_1_wa_reg));
  regfile_main main_1 (
    .Read_Register_1_a0c8cd62(instruction_decoder_1_rs), .Read_Register_2_6a35ea3b(instruction_decoder_1_rt),
    .Write_Register_a5712683(instruction_decoder_1_rd), .Write_Data_73679b02(wa_value_1_wa_reg),
    .Write_Enable_cb4a62c6(controller_1_we_reg), .Clock(CLOCK),
    .Read_Data_1_d638ea5b(main_1_read_data_1_d638ea5b), .Read_Data_2_45f3f23e(rd),
    .L_s0_Value_319056dc(L_s0_Value_555821f6), .L_s1_Value_178742e2(L_s1_Value_bb868b5b),
    .L_s2_Value_c4d9ac04(L_s2_Value_1029e135), .L_ra_Value_229931e7(L_ra_Value_3ae5280b),
    .L_sp_Value_102b2bfe(L_sp_Value_256d6ed0));
  alu_main main_2 (
    .Switch(controller_1_s_alu), .X(main_1_read_data_1_d638ea5b), .Equal(EQUAL), .Result(R),
    .Y(multiplexer_2_out), .Result_2_c6eb2740(R2));
  Multiplexer #(.width(16), .enable("false")) multiplexer_2 (
    .in0(rd), .in1(IMM), .out(multiplexer_2_out), .sel(controller_1_s_y));
  mem_main MEM (.Address(R), .Write_Data(rd), .Write_En(controller_1_we_mem), .Clock(CLOCK), .Read_Data(M));
  Register #(.width(16)) L_HI_108849eb (
    .D(R2), .en(controller_1_we_hi), .clk(CLOCK), .Q(L_HI_Value_4d3aacc1));  // open: clr
  Register #(.width(16)) L_LO_6db75bec (
    .D(multiplexer_3_out), .en(controller_1_we_lo), .clk(CLOCK), .Q(L_LO_Value_6d74149f));  // open: clr
  Multiplexer #(.width(16), .enable("false")) multiplexer_3 (
    .in0(R), .in1(IMM), .out(multiplexer_3_out), .sel(controller_1_s_lo));

  // Other names for the same wires on the sheet: clk = CLOCK; fetch_addr[15:0] = FETCH_ADDRESS;
  //   HI[15:0] = L_HI_Value_4d3aacc1; LO[15:0] = L_LO_Value_6d74149f; ra[15:0] = L_ra_Value_3ae5280b;
  //   s0[15:0] = L_s0_Value_555821f6; s1[15:0] = L_s1_Value_bb868b5b; s2[15:0] = L_s2_Value_1029e135;
  //   sp[15:0] = L_sp_Value_256d6ed0

  // Notes on the sheet:
  //   Output
  //   These are outputs/inputs from run.circ
  //   Inputs
  //   These are DEBUG/TEST outputs from your circuit.
endmodule

module Controller (
  input  [3:0] opcode,
  input  [2:0] funct,
  input  equal,
  output [2:0] S_IMM,
  output S_RD,
  output S_RT,
  output WE_REG,
  output [2:0] S_PC,
  output S_PC_BC,
  output [3:0] S_WA_REG,
  output S_Y,
  output S_LO,
  output WE_HI,
  output WE_MEM,
  output WE_LO,
  output [2:0] S_ALU
);

  wire and_1_out, and_2_out, and_5_out, and_6_out, nand_1_out, nor_1_out, nor_2_out, or_2_out, xor_1_out,
       xor_2_out;
  wire [2:0] multiplexer_2_out, multiplexer_3_out, multiplexer_4_out;

  or or_1 (S_RT, opcode[2], opcode[3]);
  and and_1 (and_1_out, ~opcode[0], opcode[3]);  // AND_Gate
  xor xor_1 (xor_1_out, opcode[1], opcode[3]);
  nand nand_1 (nand_1_out, funct[0], funct[1], funct[2]);
  and and_2 (and_2_out, nand_1_out, nor_1_out);
  nor nor_1 (nor_1_out, opcode[0], opcode[1], opcode[2], opcode[3]);
  and and_3 (WE_HI, nor_1_out, ~nand_1_out);  // AND_Gate
  nor nor_2 (nor_2_out, ~opcode[0], opcode[1], opcode[2], opcode[3]);  // NOR_Gate
  and and_4 (WE_MEM, opcode[0], opcode[1], ~opcode[2], opcode[3]);  // AND_Gate
  and and_5 (and_5_out, opcode[1], ~opcode[2]);  // AND_Gate
  or or_2 (or_2_out, and_5_out, and_6_out);
  and and_6 (and_6_out, ~opcode[0], opcode[2]);  // AND_Gate
  xor xor_2 (xor_2_out, opcode[0], opcode[1]);
  and and_7 (S_RD, xor_2_out, ~opcode[3], ~opcode[2]);  // AND_Gate
  nor nor_3 (S_IMM[0], opcode[1], opcode[2]);
  or or_3 (S_IMM[2], opcode[0], S_RT);
  and and_8 (S_PC[0], ~opcode[3], S_WA_REG[0]);  // AND_Gate
  xor xor_3 (S_WA_REG[0], opcode[1], opcode[2]);
  not not_1 (S_WA_REG[2], opcode[1]);
  or or_4 (WE_REG, and_1_out, xor_1_out, and_2_out);
  or or_5 (WE_LO, WE_HI, nor_2_out);
  Multiplexer #(.width(3), .enable("false")) multiplexer_1 (
    .in0(multiplexer_2_out), .in1(3'b010), .out(S_ALU), .sel(or_2_out));
  Multiplexer #(.width(3), .enable("false")) multiplexer_2 (
    .in0(multiplexer_3_out), .in1(3'b110), .out(multiplexer_2_out), .sel(opcode[2]));
  Multiplexer #(.width(3), .enable("false")) multiplexer_3 (
    .in0(multiplexer_4_out), .in1(3'b100), .out(multiplexer_3_out), .sel(opcode[0]));
  Multiplexer #(.width(3), .enable("false")) multiplexer_4 (
    .in0(funct), .in1(3'b011), .out(multiplexer_4_out), .sel(opcode[3]));
  xor xor_4 (S_PC_BC, equal, opcode[0]);
  not not_2 (S_PC[1], opcode[1]);
  or or_6 (S_Y, opcode[1], opcode[3]);

  assign S_IMM[1] = opcode[3];
  assign S_LO = opcode[0];
  assign S_PC[2] = opcode[0];
  assign {S_WA_REG[3], S_WA_REG[1]} = {opcode[0], opcode[3]};
endmodule

module Instruction_decoder (
  input  [15:0] Instruction,
  input  [2:0] S_IMM,
  input  S_RD,
  input  S_RT,
  output [2:0] funct,
  output [2:0] rt,
  output [2:0] rs,
  output [2:0] rd,
  output [3:0] opcode,
  output [15:0] immediate
);

  wire [9:0] bit_extender_1_out, multiplexer_3_out;
  wire [15:0] bit_extender_2_out, bit_extender_3_out, multiplexer_4_out;

  Multiplexer #(.width(3), .enable("false")) multiplexer_1 (.in0(Instruction[5:3]), .in1(rd), .out(rt), .sel(S_RT));
  Multiplexer #(.width(3), .enable("false")) multiplexer_2 (
    .in0(Instruction[11:9]), .in1({1'b0, Instruction[11:10]}), .out(rd), .sel(S_RD));
  Multiplexer #(.width(10), .enable("false")) multiplexer_3 (
    .in0(Instruction[9:0]), .in1(bit_extender_1_out), .out(multiplexer_3_out), .sel(S_IMM[2]));
  assign bit_extender_1_out = {{4{Instruction[5]}}, Instruction[5:0]};  // Bit_Extender bit_extender_1
  assign bit_extender_2_out = {{6{1'b0}}, bit_extender_1_out};  // Bit_Extender bit_extender_2
  assign bit_extender_3_out = {{6{multiplexer_3_out[9]}}, multiplexer_3_out};  // Bit_Extender bit_extender_3
  Multiplexer #(.width(16), .enable("false")) multiplexer_4 (
    .in0({Instruction[9:0], {6{1'b0}}}), .in1(bit_extender_2_out), .out(multiplexer_4_out), .sel(S_IMM[1]));
  Multiplexer #(.width(16), .enable("false")) multiplexer_5 (
    .in0(bit_extender_3_out), .in1(multiplexer_4_out), .out(immediate), .sel(S_IMM[0]));

  assign funct = Instruction[2:0];
  assign opcode = Instruction[15:12];
  assign rs = Instruction[8:6];

  // Other names for the same wires on the sheet: prt[2:0] = Instruction[5:3]; imm[15:0] = immediate
endmodule

module PC_Value (
  input  [15:0] PC2_in,
  input  [15:0] PC_in,
  input  [15:0] IMM,
  input  [2:0] S_PC,
  input  [15:0] JUMP_REG,
  input  S_PC_BC,
  output [15:0] PC_out
);

  wire [15:0] adder_1_out, BRANCH, multiplexer_1_out, multiplexer_4_out;

  Adder #(.width(16)) adder_1 (.a(PC_in), .b(IMM), .out(adder_1_out));  // open: cin, cout
  Multiplexer #(.width(16), .enable("false")) multiplexer_1 (
    .in0({PC_in[15:10], IMM[9:0]}), .in1(JUMP_REG), .out(multiplexer_1_out), .sel(S_PC[2]));
  Multiplexer #(.width(16), .enable("false")) multiplexer_2 (
    .in0(PC2_in), .in1(adder_1_out), .out(BRANCH), .sel(S_PC_BC));
  Multiplexer #(.width(16), .enable("false")) multiplexer_3 (
    .in0(PC2_in), .in1(multiplexer_4_out), .out(PC_out), .sel(S_PC[0]));
  Multiplexer #(.width(16), .enable("false")) multiplexer_4 (
    .in0(multiplexer_1_out), .in1(BRANCH), .out(multiplexer_4_out), .sel(S_PC[1]));

  // Other names for the same wires on the sheet: PC[15:0] = PC_in; JUMP[15:0] = JUMP_REG; PC2[15:0] = PC2_in
endmodule

module WA_Value (
  input  [15:0] R,
  input  [15:0] PC2,
  input  [15:0] M,
  input  [15:0] HI,
  input  [15:0] LO,
  input  [3:0] S_WA_REG,
  output [15:0] WA_REG
);

  wire [15:0] multiplexer_1_out, multiplexer_2_out, multiplexer_3_out;

  Multiplexer #(.width(16), .enable("false")) multiplexer_1 (
    .in0(HI), .in1(LO), .out(multiplexer_1_out), .sel(S_WA_REG[3]));
  Multiplexer #(.width(16), .enable("false")) multiplexer_2 (
    .in0(PC2), .in1(multiplexer_3_out), .out(multiplexer_2_out), .sel(S_WA_REG[1]));
  Multiplexer #(.width(16), .enable("false")) multiplexer_3 (
    .in0(M), .in1(multiplexer_1_out), .out(multiplexer_3_out), .sel(S_WA_REG[2]));
  Multiplexer #(.width(16), .enable("false")) multiplexer_4 (
    .in0(R), .in1(multiplexer_2_out), .out(WA_REG), .sel(S_WA_REG[0]));
endmodule
