// Logisim project cpu.circ as structural Verilog: 6 circuits, main circuit main
module main (
  input  clock,
  input  [15:0] INSTRUCTION,
  output [15:0] FETCH_ADDRESS,
  output [15:0] ra,
  output [15:0] s0,
  output [15:0] s1,
  output [15:0] s2,
  output [15:0] sp,
  output [15:0] hii,
  output [15:0] loo
);

  wire alu_1_equal, and_1_out, and_2_out, and_3_out, controle_1_aluop0, controle_1_aluop1, controle_1_andd,
       controle_1_bnq, controle_1_branch, controle_1_hi, controle_1_jump, controle_1_jumpreg, controle_1_lo,
       controle_1_luiii, controle_1_memwrite, controle_1_orr, controle_1_regwrite, not_1_out, or_1_out,
       or_2_out;
  wire [1:0] controle_1_alusrc, controle_1_memtoreg, controle_1_regdst;
  wire [2:0] aluop_1_out_4, multiplexer_1_out, multiplexer_3_out, multiplexer_4_out;
  wire [5:0] adder_1_out_2;
  wire [9:0] adder_1_out;
  wire [15:0] adder_2_out, alu_1_result1, alu_1_result2, bit_extender_1_out, bit_extender_2_out,
       mem_1_read_data, multiplexer_2_out, multiplexer_5_out, multiplexer_6_out, multiplexer_7_out,
       multiplexer_8_out, multiplexer_9_out, multiplexer_10_out, multiplexer_11_out, regfile_1_r1,
       regfile_1_r2, shifter_1_out, shifter_2_out;

  Register #(.width(16)) pc (.D(multiplexer_10_out), .clk(clock), .Q(FETCH_ADDRESS));  // open: en, clr
  controle controle_1 (
    .in_1(INSTRUCTION[15:12]), .REGDST(controle_1_regdst), .ALUSRC(controle_1_alusrc),
    .MEMTOREG(controle_1_memtoreg), .REGWRITE(controle_1_regwrite), .MEMWRITE(controle_1_memwrite),
    .BRANCH(controle_1_branch), .Jump(controle_1_jump), .ALUOP1(controle_1_aluop1),
    .ALUOP0(controle_1_aluop0), .jumpreg(controle_1_jumpreg), .BNQ(controle_1_bnq), .orr(controle_1_orr),
    .andd(controle_1_andd), .hi(controle_1_hi), .lo(controle_1_lo), .luiii(controle_1_luiii));  // open: MEMREAD
  Adder #(.width(16)) adder_1 (.a(FETCH_ADDRESS), .b(16'h2), .out({adder_1_out_2, adder_1_out}));  // open: cin, cout
  Multiplexer #(.select(2), .width(3), .enable("false")) multiplexer_1 (
    .in0(INSTRUCTION[11:9]), .in1(INSTRUCTION[5:3]), .in2(INSTRUCTION[12:10]), .out(multiplexer_1_out),
    .sel(controle_1_regdst));  // open: in3
  assign bit_extender_1_out = {{6{1'b0}}, INSTRUCTION[9:0]};  // Bit_Extender bit_extender_1
  Shifter #(.width(16)) shifter_1 (.in(bit_extender_1_out), .\dist (4'b0110), .out(shifter_1_out));
  regfile regfile_1 (
    .clock(clock), .rr1(INSTRUCTION[8:6]), .wenable(controle_1_regwrite), .wreg(multiplexer_1_out),
    .wdata(multiplexer_9_out), .rr2(INSTRUCTION[5:3]), .ra(ra), .s0(s0), .r1(regfile_1_r1), .s1(s1), .s2(s2),
    .r2(regfile_1_r2), .sp(sp));
  assign bit_extender_2_out = {{10{1'b0}}, INSTRUCTION[5:0]};  // Bit_Extender bit_extender_2
  Multiplexer #(.select(2), .width(16), .enable("false")) multiplexer_2 (
    .in0(bit_extender_2_out), .in1(regfile_1_r2), .in2(shifter_2_out), .out(multiplexer_2_out),
    .sel(controle_1_alusrc));  // open: in3
  aluop aluop_1 (.OP1(controle_1_aluop1), .OP0(controle_1_aluop0), .in_3(INSTRUCTION[2:0]), .out_4(aluop_1_out_4));
  and and_1 (and_1_out, INSTRUCTION[0], INSTRUCTION[1], INSTRUCTION[2]);
  Multiplexer #(.width(3), .enable("false")) multiplexer_3 (
    .in0(aluop_1_out_4), .in1(multiplexer_4_out), .out(multiplexer_3_out), .sel(controle_1_orr));
  Multiplexer #(.width(3), .enable("false")) multiplexer_4 (
    .in0(3'b100), .in1(3'b011), .out(multiplexer_4_out), .sel(controle_1_andd));
  or or_1 (or_1_out, and_1_out, controle_1_luiii);
  alu alu_1 (
    .switch(multiplexer_3_out), .x(regfile_1_r1), .y(multiplexer_2_out), .result1(alu_1_result1),
    .equal(alu_1_equal), .result2(alu_1_result2));
  Multiplexer #(.width(16), .enable("false")) multiplexer_5 (
    .in0(alu_1_result2), .in1(shifter_1_out), .out(multiplexer_5_out), .sel(controle_1_luiii));
  Register #(.width(16)) lo (.D(multiplexer_5_out), .en(or_1_out), .clk(clock), .Q(loo));  // open: clr
  Register #(.width(16)) hi (.D(alu_1_result1), .en(and_1_out), .clk(clock), .Q(hii));  // open: clr
  Adder #(.width(16)) adder_2 (
    .a({adder_1_out_2, adder_1_out}), .b(shifter_2_out), .out(adder_2_out));  // open: cin, cout
  Shifter #(.width(16)) shifter_2 (.in(bit_extender_2_out), .\dist (4'b0001), .out(shifter_2_out));
  Multiplexer #(.width(16), .enable("false")) multiplexer_6 (
    .in0(loo), .in1(hii), .out(multiplexer_6_out), .sel(controle_1_hi));
  and and_2 (and_2_out, controle_1_branch, alu_1_equal);
  Multiplexer #(.width(16), .enable("false")) multiplexer_7 (
    .in0({adder_1_out_2, adder_1_out}), .in1(adder_2_out), .out(multiplexer_7_out), .sel(or_2_out));
  or or_2 (or_2_out, and_2_out, and_3_out);
  and and_3 (and_3_out, not_1_out, controle_1_bnq);
  not not_1 (not_1_out, alu_1_equal);
  Multiplexer #(.width(16), .enable("false")) multiplexer_8 (
    .in0(multiplexer_7_out), .in1({adder_1_out_2, INSTRUCTION[9:0]}), .out(multiplexer_8_out),
    .sel(controle_1_jump));
  Mem mem_1 (
    .Address(alu_1_result1), .Write_Data(regfile_1_r2), .Write_En(controle_1_memwrite), .Clock(clock),
    .Read_Data(mem_1_read_data));
  Multiplexer #(.width(16), .enable("false")) multiplexer_9 (
    .in0(multiplexer_11_out), .in1(multiplexer_6_out), .out(multiplexer_9_out), .sel(controle_1_lo));
  Multiplexer #(.width(16), .enable("false")) multiplexer_10 (
    .in0(multiplexer_8_out), .in1(alu_1_result1), .out(multiplexer_10_out), .sel(controle_1_jumpreg));
  Multiplexer #(.select(2), .width(16), .enable("false")) multiplexer_11 (
    .in0(mem_1_read_data), .in1(alu_1_result1), .in2({adder_1_out_2, adder_1_out}), .out(multiplexer_11_out),
    .sel(controle_1_memtoreg));  // open: in3

  // Other names for the same wires on the sheet: OPCODE[15:0] = INSTRUCTION
endmodule

module regfile (
  input  clock,
  input  [2:0] rr1,
  input  wenable,
  input  [2:0] wreg,
  input  [15:0] wdata,
  input  [2:0] rr2,
  output [15:0] ra,
  output [15:0] s0,
  output [15:0] r1,
  output [15:0] s1,
  output [15:0] s2,
  output [15:0] r2,
  output [15:0] sp
);

  wire and_1_out, and_2_out, and_3_out, and_4_out, and_5_out, and_6_out, and_7_out, and_8_out,
       demultiplexer_1_out0, demultiplexer_1_out1, demultiplexer_1_out2, demultiplexer_1_out3,
       demultiplexer_1_out4, demultiplexer_1_out5, demultiplexer_1_out6, demultiplexer_1_out7;
  wire [15:0] register_1_q, register_6_q, register_7_q;

  Demultiplexer #(.select(3), .enable("false")) demultiplexer_1 (
    .out0(demultiplexer_1_out0), .out1(demultiplexer_1_out1), .out2(demultiplexer_1_out2),
    .out3(demultiplexer_1_out3), .out4(demultiplexer_1_out4), .out5(demultiplexer_1_out5),
    .out6(demultiplexer_1_out6), .out7(demultiplexer_1_out7), .in(1'b1), .sel(wreg));
  Register #(.width(16)) register_1 (.D(wdata), .en(and_1_out), .Q(register_1_q));  // open: clk, clr
  and and_1 (and_1_out, wenable, demultiplexer_1_out0);
  Register #(.width(16)) register_2 (.D(wdata), .en(and_2_out), .clk(clock), .Q(ra));  // open: clr
  and and_2 (and_2_out, wenable, demultiplexer_1_out1);
  Register #(.width(16)) register_3 (.D(wdata), .en(and_3_out), .clk(clock), .Q(s0));  // open: clr
  and and_3 (and_3_out, wenable, demultiplexer_1_out2);
  Register #(.width(16)) register_4 (.D(wdata), .en(and_4_out), .clk(clock), .Q(s1));  // open: clr
  and and_4 (and_4_out, wenable, demultiplexer_1_out3);
  Register #(.width(16)) register_5 (.D(wdata), .en(and_5_out), .clk(clock), .Q(s2));  // open: clr
  and and_5 (and_5_out, wenable, demultiplexer_1_out4);
  Register #(.width(16)) register_6 (.D(wdata), .en(and_6_out), .clk(clock), .Q(register_6_q));  // open: clr
  and and_6 (and_6_out, wenable, demultiplexer_1_out5);
  Register #(.width(16)) register_7 (.D(wdata), .en(and_7_out), .clk(clock), .Q(register_7_q));  // open: clr
  and and_7 (and_7_out, wenable, demultiplexer_1_out6);
  Register #(.width(16)) register_8 (.D(wdata), .en(and_8_out), .clk(clock), .Q(sp));  // open: clr
  and and_8 (and_8_out, wenable, demultiplexer_1_out7);
  Multiplexer #(.select(3), .width(16), .enable("false")) multiplexer_1 (
    .in0(register_1_q), .in1(ra), .in2(s0), .in3(s1), .in4(s2), .in5(register_6_q), .in6(register_7_q),
    .in7(sp), .out(r1), .sel(rr1));
  Multiplexer #(.select(3), .width(16), .enable("false")) multiplexer_2 (
    .in0(register_1_q), .in1(ra), .in2(s0), .in3(s1), .in4(s2), .in5(register_6_q), .in6(register_7_q),
    .in7(sp), .out(r2), .sel(rr2));
endmodule

module alu (
  input  [2:0] switch,
  input  [15:0] x,
  input  [15:0] y,
  output [15:0] result1,
  output equal,
  output [15:0] result2
);

  wire subtractor_1_bout;
  wire [15:0] adder_1_out, and_1_out, bit_extender_1_out, multiplier_1_out, or_1_out, shifter_1_out,
       shifter_2_out, subtractor_1_out, xor_1_out;

  Subtractor #(.width(16)) subtractor_1 (.a(x), .b(y), .out(subtractor_1_out), .bout(subtractor_1_bout));  // open: bin
  Shifter #(.width(16)) shifter_1 (.in(x), .\dist (y[3:0]), .out(shifter_1_out));
  Shifter #(.width(16), .shift("lr")) shifter_2 (.in(x), .\dist (y[3:0]), .out(shifter_2_out));
  Adder #(.width(16)) adder_1 (.a(x), .b(y), .out(adder_1_out));  // open: cin, cout
  assign and_1_out = x & y;  // AND_Gate and_1, 16 bits wide
  assign or_1_out = x | y;  // OR_Gate or_1, 16 bits wide
  assign bit_extender_1_out = {{15{1'b0}}, subtractor_1_bout};  // Bit_Extender bit_extender_1
  Multiplier #(.width(16)) multiplier_1 (.a(x), .b(y), .out(multiplier_1_out), .cout(result2));  // open: cin
  assign xor_1_out = x ^ y;  // XOR_Gate xor_1, 16 bits wide
  Multiplexer #(.select(3), .width(16), .enable("false")) multiplexer_1 (
    .in0(shifter_1_out), .in1(shifter_2_out), .in2(adder_1_out), .in3(and_1_out), .in4(or_1_out),
    .in5(xor_1_out), .in6(bit_extender_1_out), .in7(multiplier_1_out), .out(result1), .sel(switch));
  nor nor_1 (equal, subtractor_1_out[0], subtractor_1_out[1], subtractor_1_out[2], subtractor_1_out[3], subtractor_1_out[4], subtractor_1_out[5], subtractor_1_out[6], subtractor_1_out[7], subtractor_1_out[8], subtractor_1_out[9], subtractor_1_out[10], subtractor_1_out[11], subtractor_1_out[12], subtractor_1_out[13], subtractor_1_out[14], subtractor_1_out[15]);
endmodule

module aluop (
  input  OP1,
  input  OP0,
  input  [2:0] in_3,
  output [2:0] out_4
);

  wire and_1_out, not_1_out;

  and and_1 (and_1_out, OP1, in_3[2]);
  not not_1 (not_1_out, OP1);
  and and_2 (out_4[0], OP1, in_3[0]);
  or or_1 (out_4[2], OP0, and_1_out);
  or or_2 (out_4[1], not_1_out, in_3[1], OP0);
endmodule

module controle (
  input  [3:0] in_1,
  output [1:0] REGDST,
  output [1:0] ALUSRC,
  output [1:0] MEMTOREG,
  output REGWRITE,
  output MEMREAD,
  output MEMWRITE,
  output BRANCH,
  output Jump,
  output ALUOP1,
  output ALUOP0,
  output jumpreg,
  output BNQ,
  output orr,
  output andd,
  output hi,
  output lo,
  output luiii
);

  wire addi_out, ori_out, slti_out;

  and Tipor (ALUOP1, ~in_1[3], ~in_1[2], ~in_1[1], ~in_1[0]);  // AND_Gate
  and lw (MEMREAD, in_1[3], ~in_1[2], in_1[1], ~in_1[0]);  // AND_Gate
  and sw (ALUSRC[1], in_1[3], ~in_1[2], in_1[1], in_1[0]);  // AND_Gate
  and beq (BRANCH, ~in_1[3], in_1[2], ~in_1[1], ~in_1[0]);  // AND_Gate
  and juump (Jump, ~in_1[3], ~in_1[2], in_1[1], ~in_1[0]);  // AND_Gate
  and juumpreg (jumpreg, ~in_1[3], ~in_1[2], in_1[1], in_1[0]);  // AND_Gate
  and bnnq (BNQ, ~in_1[3], in_1[2], ~in_1[1], in_1[0]);  // AND_Gate
  and addi (addi_out, ~in_1[3], in_1[2], in_1[1], ~in_1[0]);  // AND_Gate
  and slti (slti_out, ~in_1[3], in_1[2], in_1[1], in_1[0]);  // AND_Gate
  and ori (ori_out, in_1[3], ~in_1[2], ~in_1[1], in_1[0]);  // AND_Gate
  and andi (andd, in_1[3], ~in_1[2], ~in_1[1], ~in_1[0]);  // AND_Gate
  and mfhi (hi, in_1[3], in_1[2], ~in_1[1], ~in_1[0]);  // AND_Gate
  and mflo (lo, in_1[3], in_1[2], ~in_1[1], in_1[0]);  // AND_Gate
  and lui (luiii, ~in_1[3], ~in_1[2], ~in_1[1], in_1[0]);  // AND_Gate
  or or_1 (REGDST[0], lo, jumpreg, ALUOP1, hi);
  or or_2 (MEMTOREG[0], jumpreg, MEMREAD);
  or or_3 (ALUSRC[0], ori_out, addi_out, MEMREAD, slti_out, jumpreg, ALUSRC[1], andd);
  or or_4 (REGWRITE, ALUOP1, Jump, addi_out, MEMREAD, jumpreg);
  buf or_5 (ALUOP0, slti_out);  // OR_Gate
  or or_6 (orr, ori_out, andd);

  assign MEMTOREG[1] = Jump;
  assign MEMWRITE = ALUSRC[1];
  assign REGDST[1] = Jump;
endmodule

module Mem (
  input  [15:0] Address,
  input  [15:0] Write_Data,
  input  Write_En,
  input  Clock,
  output [15:0] Read_Data
);

  RAM #(.addrWidth(14), .dataWidth(16), .trigger("falling"), .databus("bibus")) ram_1 (
    .addr(Address[14:1]), .we(Write_En), .oe(1'b1), .clk(Clock), .din(Write_Data), .dout(Read_Data));
endmodule
