// Logisim project alu-logic.circ as structural Verilog: 1 circuit, main circuit main
module main (
  output [7:0] Test_6fcbf03b,
  output Equal,
  output [15:0] Result,
  output [15:0] Result_2_949f821f
);

  wire clock_1_out;
  wire [2:0] rom_2_data;
  wire [7:0] adder_1_out;
  wire [15:0] rom_1_data, rom_3_data;

  Register register_1 (.D(adder_1_out), .en(1'b1), .clk(clock_1_out), .Q(Test_6fcbf03b));  // open: clr
  Clock clock_1 (.out(clock_1_out));
  Adder adder_1 (.a(8'h1), .b(Test_6fcbf03b), .out(adder_1_out));  // open: cin, cout
  ROM #(.dataWidth(16)) rom_1 (.addr(Test_6fcbf03b), .data(rom_1_data));
  ROM #(.dataWidth(3)) rom_2 (.addr(Test_6fcbf03b), .data(rom_2_data));
  alu_main main_1 (
    .Switch(rom_2_data), .X(rom_1_data), .Equal(Equal), .Result(Result), .Y(rom_3_data),
    .Result_2_c6eb2740(Result_2_949f821f));
  ROM #(.dataWidth(16)) rom_3 (.addr(Test_6fcbf03b), .data(rom_3_data));

  // Notes on the sheet:
  //   contents of rom_1 (hex, n*v repeats v):
  //   ffff 5555 ffff 0 aaaa dffe dead ffff 4321
  //   contents of rom_2 (hex, n*v repeats v):
  //   3 3 3 4 4 4 5 5 5
  //   YOUR ALU SHOULD FIT HERE
  //   There should be no blue/red wires here, and the result shouldn't be x's.
  //   contents of rom_3 (hex, n*v repeats v):
  //   0 aaaa abcd ffff 5555 0 dead 5555 abcd
endmodule
