// Logisim project regfile.circ as structural Verilog: 1 circuit, main circuit main
module main (
  input  [2:0] Read_Register_1,
  input  [2:0] Read_Register_2,
  input  [2:0] Write_Register,
  input  [15:0] Write_Data,
  input  Write_Enable,
  input  Clock,
  output [15:0] s0_Value,
  output [15:0] s1_Value,
  output [15:0] s2_Value,
  output [15:0] ra_Value,
  output [15:0] sp_Value,
  output [15:0] Read_Data_1,
  output [15:0] Read_Data_2
);


  // Other names for the same wires on the sheet: clk = Clock; read_data1[15:0] = Read_Data_1;
  //   read_data2[15:0] = Read_Data_2; read_reg1[2:0] = Read_Register_1; read_reg2[2:0] = Read_Register_2;
  //   write_en = Write_Enable; write_reg[2:0] = Write_Register

  // Notes on the sheet:
  //   INPUTS to your circuit
  //   DON'T CHANGE THE LOCATIONS OF THE INPUTS AND OUTPUTS!
  //   These are DEBUG/TEST outputs from your circuit.
  //   OUTPUTS from your circuit
endmodule
